# Fritzing sketch simonsez (saved by Fritzing 0.9.3b)
breadboards: 1

parts:
  Part1 = Arduino Uno (Rev3)
  LED1 = LED - 5mm [color="Blue (505nm)" package="5 mm [THT]"]
  R1 = Resistor [tolerance=±5% resistance=220 package=THT]
  S1 = Pushbutton [package="[THT]"]
  R2 = Resistor [tolerance=±5% resistance=100 package=THT]
  R3 = Resistor [tolerance=±5% resistance=100 package=THT]
  R4 = Resistor [tolerance=±5% resistance=100 package=THT]
  R5 = Resistor [tolerance=±5% resistance=100 package=THT]
  LED2 = LED - 5mm [color="Green (560nm)" package="5 mm [THT]"]
  LED3 = LED - 5mm [color="Yellow (574nm)" package="5 mm [THT]"]
  LED4 = LED - 5mm [color="Red (660nm)" package="5 mm [THT]"]
  S2 = Pushbutton [package="[THT]"]
  S3 = Pushbutton [package="[THT]"]
  S4 = Pushbutton [package="[THT]"]
  R6 = Resistor [tolerance=±5% resistance=220 package=THT]
  R7 = Resistor [tolerance=±5% resistance=220 package=THT]
  R8 = Resistor [tolerance=±5% resistance=220 package=THT]
  J1 = Piezo Speaker

nets:
  N1: Part1.D10_PWM/SS, LED4.anode
  N2: Part1.D11_PWM/MOSI, LED3.anode
  N3: Part1.D12/MISO, LED2.anode
  N4: Part1.D13/SCK, LED1.anode
  N5: Part1.D3_PWM, J1.pin2
  N6: Part1.D4, R4.Pin_0, S4.Pin_1, S4.Pin_2
  N7: Part1.D5_PWM, R2.Pin_0, S3.Pin_1, S3.Pin_2
  N8: Part1.D6_PWM, R5.Pin_0, S2.Pin_1, S2.Pin_2
  N9: Part1.D7, S1.Pin_1, S1.Pin_2, R3.Pin_0
  N10: Part1.5V, S1.Pin_3, S1.Pin_4, S2.Pin_3, S2.Pin_4, S3.Pin_3, S3.Pin_4, S4.Pin_3, S4.Pin_4
  N11: Part1.GND, R1.Pin_1, R2.Pin_1, R3.Pin_1, R4.Pin_1, R5.Pin_1, R6.Pin_1, R7.Pin_1, R8.Pin_1, J1.pin1
  N12: LED1.cathode, R1.Pin_0
  N13: LED2.cathode, R6.Pin_0
  N14: LED3.cathode, R7.Pin_0
  N15: LED4.cathode, R8.Pin_0

notes:
  Simonsez original prototyped circuitry
  This is my first attempt at using fritzing, so I am sure it can be done better. The wires on the LEDs have been twisted to better reflect cathode and anode connections. In real life you can just flip the LED to the corresponding breadboard peg without having to twist the wires. (DONT TWIST THE WIRES ON THE LEDS)
